// Digital circuit Digital.dig as structural Verilog
module Digital (
  input  Add_Out,
  input  Sub_Out,
  input  Or_Out,
  input  And_Out,
  input  Xor_Out,
  input  RShift_Out,
  input  RAM___ROM
);

  wire and_1_out, and_2_out, Clock_out, decoder_1_out_0, decoder_1_out_1, decoder_1_out_2, decoder_1_out_3,
       decoder_1_out_4, decoder_1_out_5, decoder_1_out_6, decoder_2_out_0, decoder_2_out_1, decoder_2_out_2,
       decoder_2_out_3, decoder_2_out_4, decoder_2_out_5, decoder_2_out_6, decoder_2_out_7, decoder_2_out_8,
       decoder_3_out_0, decoder_3_out_1, decoder_3_out_2, decoder_4_out_0, decoder_4_out_1, decoder_4_out_2,
       decoder_4_out_3, decoder_5_out_0, decoder_5_out_1, decoder_5_out_2, decoder_5_out_3, or_1_out,
       or_2_out, pulldown_1_out, pulldown_2_out, pulldown_3_out, pulldown_6_out, pulldown_7_out,
       pullup_1_out, undriven;
  wire [3:0] a1_q, a1_q_2, a2_q, a2_q_2, Microcode_d_2;
  wire [7:0] add_1_s, and_3_out, decoder_3_out_3, dh_q, dl_q, driver_6_out, or_3_out, r1_q, r2_q, r3_q, r4_q,
       Right_shift_out, sub_1_s, xor_1_out;
  wire [11:0] Microcode_d;
  wire [15:0] ah_al_q, DC_out_2, PC_out_2, SP_out_2;
  wire [15:8] driver_5_out;

  Decoder #(.Selector_Bits(4)) decoder_1 (
    .sel(Microcode_d_2), .out_0(decoder_1_out_0), .out_1(decoder_1_out_1), .out_2(decoder_1_out_2),
    .out_3(decoder_1_out_3), .out_4(decoder_1_out_4), .out_5(decoder_1_out_5), .out_6(decoder_1_out_6));  // open: out_7, out_8, out_9, out_10, out_11, out_12, out_13, out_14, out_15
  Decoder #(.Selector_Bits(4)) decoder_2 (
    .sel(Microcode_d[11:8]), .out_0(decoder_2_out_0), .out_1(decoder_2_out_1), .out_2(decoder_2_out_2),
    .out_3(decoder_2_out_3), .out_4(decoder_2_out_4), .out_5(decoder_2_out_5), .out_6(decoder_2_out_6),
    .out_7(decoder_2_out_7), .out_8(decoder_2_out_8));  // open: out_9, out_10, out_11, out_12, out_13, out_14, out_15
  Decoder #(.Selector_Bits(2)) decoder_3 (
    .sel(Microcode_d[7:6]), .out_0(decoder_3_out_0), .out_1(decoder_3_out_1), .out_2(decoder_3_out_2),
    .out_3(decoder_3_out_3[0]));
  Decoder #(.Selector_Bits(3)) decoder_4 (
    .sel(Microcode_d[5:3]), .out_0(decoder_4_out_0), .out_1(decoder_4_out_1), .out_2(decoder_4_out_2),
    .out_3(decoder_4_out_3));  // open: out_4, out_5, out_6, out_7
  Decoder #(.Selector_Bits(3)) decoder_5 (
    .sel(Microcode_d[2:0]), .out_0(decoder_5_out_0), .out_1(decoder_5_out_1), .out_2(decoder_5_out_2),
    .out_3(decoder_5_out_3));  // open: out_4, out_5, out_6, out_7
  LED PC_Out (.in(decoder_3_out_0));
  LED PC_Count (.in(decoder_5_out_0));
  LED PC_In (.in(decoder_4_out_0));
  LED r1_Out (.in(decoder_1_out_0));
  LED r1_In (.in(decoder_2_out_0));
  LED r2_Out (.in(decoder_1_out_1));
  LED r2_In (.in(decoder_2_out_1));
  LED r3_Out (.in(decoder_1_out_2));
  LED r3_In (.in(decoder_2_out_2));
  LED r4_Out (.in(decoder_1_out_3));
  LED r4_In (.in(decoder_2_out_3));
  LED dh_In (.in(decoder_2_out_5));
  LED dh_dl_Out (.in(decoder_3_out_3[0]));
  LED dl_In (.in(decoder_2_out_6));
  LED DC_Out (.in(decoder_3_out_1));
  LED PC_Count_2 (.in(decoder_5_out_1));
  LED DC_In (.in(decoder_4_out_1));
  LED RAM_In (.in(decoder_2_out_4));
  LED Mem_Out (.in(decoder_1_out_4));
  LED SP_Out (.in(decoder_3_out_2));
  LED SP_Inc (.in(decoder_5_out_2));
  LED SP_Dec (.in(decoder_5_out_3));
  LED SP_In (.in(decoder_4_out_2));
  LED ah_Out (.in(decoder_1_out_5));
  LED al_Out (.in(decoder_1_out_6));
  LED al_ah_In (.in(decoder_4_out_3));
  Button Clock (.out(Clock_out));
  PullUp pullup_1 (.out(pullup_1_out));
  ROM #(.AddrBits(12), .Bits(16)) Microcode (.sel(pullup_1_out), .D({Microcode_d_2, Microcode_d}));  // open: A
  or or_1 (or_1_out, decoder_5_out_2, decoder_5_out_3);
  PullDown pulldown_1 (.out(pulldown_1_out));
  or or_2 (or_2_out, RAM___ROM, driver_5_out[12], driver_5_out[13], driver_5_out[14], driver_5_out[15]);
  PullDown pulldown_2 (.out(pulldown_2_out));
  CounterPreset #(.Bits(16)) PC (
    .en(decoder_5_out_0), .C(Clock_out), .dir(pulldown_3_out), .in({driver_5_out, driver_6_out}),
    .ld(decoder_4_out_0), .clr(pulldown_3_out), .out(PC_out_2));  // open: ovf
  PullDown pulldown_3 (.out(pulldown_3_out));
  Register #(.Bits(8)) r1 (.D(decoder_3_out_3), .C(Clock_out), .en(decoder_2_out_0), .Q(r1_q));
  Register #(.Bits(8)) r2 (.D(decoder_3_out_3), .C(Clock_out), .en(decoder_2_out_1), .Q(r2_q));
  Register #(.Bits(8)) r3 (.D(decoder_3_out_3), .C(Clock_out), .en(decoder_2_out_2), .Q(r3_q));
  Register #(.Bits(8)) r4 (.D(decoder_3_out_3), .C(Clock_out), .en(decoder_2_out_3), .Q(r4_q));
  Register #(.Bits(8)) dh (.D(decoder_3_out_3), .C(Clock_out), .en(decoder_2_out_5), .Q(dh_q));
  Register #(.Bits(8)) dl (.D(decoder_3_out_3), .C(Clock_out), .en(decoder_2_out_6), .Q(dl_q));
  CounterPreset #(.Bits(16)) DC (
    .en(decoder_5_out_1), .C(Clock_out), .dir(pulldown_1_out), .in({driver_5_out, driver_6_out}),
    .ld(decoder_4_out_1), .clr(pulldown_1_out), .out(DC_out_2));  // open: ovf
  ROM #(.AddrBits(16), .Bits(8)) _8_KB_ROM (.A({driver_5_out, driver_6_out}), .sel(and_1_out), .D(decoder_3_out_3));
  RAMSinglePort #(.AddrBits(16), .Bits(8)) _64_KB_RAM (
    .A({driver_5_out, driver_6_out}), .str(decoder_2_out_4), .C(Clock_out), .ld(and_2_out),
    .D(decoder_3_out_3));
  CounterPreset #(.Bits(16)) SP (
    .en(or_1_out), .C(Clock_out), .dir(decoder_5_out_3), .in({driver_5_out, driver_6_out}),
    .ld(decoder_4_out_2), .clr(pulldown_2_out), .out(SP_out_2));  // open: ovf
  Register #(.Bits(16)) ah_al (.D({driver_5_out, driver_6_out}), .C(Clock_out), .en(decoder_4_out_3), .Q(ah_al_q));
  assign decoder_3_out_3 = decoder_1_out_0 ? r1_q : 8'bz;  // Driver driver_1
  assign decoder_3_out_3 = decoder_1_out_1 ? r2_q : 8'bz;  // Driver driver_2
  assign decoder_3_out_3 = decoder_1_out_2 ? r3_q : 8'bz;  // Driver driver_3
  assign decoder_3_out_3 = decoder_1_out_3 ? r4_q : 8'bz;  // Driver driver_4
  assign driver_5_out = undriven ? dh_q : 8'bz;  // Driver driver_5
  assign driver_6_out = undriven ? dl_q : 8'bz;  // Driver driver_6
  assign {driver_5_out, driver_6_out} = decoder_3_out_1 ? DC_out_2 : 16'bz;  // Driver driver_7
  LED ROM_Selected (.in(and_1_out));
  LED RAM_Selected (.in(and_2_out));
  and and_1 (and_1_out, decoder_1_out_4, ~or_2_out);  // And
  and and_2 (and_2_out, decoder_1_out_4, or_2_out);
  assign {driver_5_out, driver_6_out} = decoder_3_out_2 ? SP_out_2 : 16'bz;  // Driver driver_8
  assign {driver_5_out, driver_6_out} = decoder_3_out_0 ? PC_out_2 : 16'bz;  // Driver driver_9
  assign decoder_3_out_3 = decoder_1_out_6 ? ah_al_q[7:0] : 8'bz;  // Driver driver_10
  assign decoder_3_out_3 = decoder_1_out_5 ? ah_al_q[15:8] : 8'bz;  // Driver driver_11
  Seven_Seg_Hex seven_seg_hex_1 (.d(driver_5_out[15:12]), .dp(1'b0));
  PullDown #(.Bits(16)) pulldown_4 (.out({driver_5_out, driver_6_out}));
  Seven_Seg_Hex seven_seg_hex_2 (.d(decoder_3_out_3[7:4]), .dp(1'b0));
  Seven_Seg_Hex seven_seg_hex_3 (.d(driver_5_out[11:8]), .dp(1'b0));
  Seven_Seg_Hex seven_seg_hex_4 (.d(decoder_3_out_3[3:0]), .dp(1'b0));
  PullDown #(.Bits(8)) pulldown_5 (.out(decoder_3_out_3));
  Seven_Seg_Hex seven_seg_hex_5 (.d(driver_6_out[7:4]), .dp(1'b0));
  Seven_Seg_Hex seven_seg_hex_6 (.d(driver_6_out[3:0]), .dp(1'b0));
  LED a1_In (.in(decoder_2_out_7));
  LED a2_In (.in(decoder_2_out_8));
  assign decoder_3_out_3 = Add_Out ? add_1_s : 8'bz;  // Driver driver_12
  assign decoder_3_out_3 = Sub_Out ? sub_1_s : 8'bz;  // Driver driver_13
  assign decoder_3_out_3 = Or_Out ? or_3_out : 8'bz;  // Driver driver_14
  assign decoder_3_out_3 = And_Out ? and_3_out : 8'bz;  // Driver driver_15
  assign decoder_3_out_3 = Xor_Out ? xor_1_out : 8'bz;  // Driver driver_16
  assign decoder_3_out_3 = RShift_Out ? Right_shift_out : 8'bz;  // Driver driver_17
  Register #(.Bits(8)) a1 (.D(decoder_3_out_3), .C(Clock_out), .en(decoder_2_out_7), .Q({a1_q_2, a1_q}));
  Register #(.Bits(8)) a2 (.D(decoder_3_out_3), .C(Clock_out), .en(decoder_2_out_8), .Q({a2_q_2, a2_q}));
  Add #(.Bits(8)) add_1 (.a({a1_q_2, a1_q}), .b({a2_q_2, a2_q}), .c_i(pulldown_6_out), .s(add_1_s));  // open: c_o
  Sub #(.Bits(8)) sub_1 (.a({a1_q_2, a1_q}), .b({a2_q_2, a2_q}), .c_i(pulldown_6_out), .s(sub_1_s));  // open: c_o
  assign or_3_out = {a2_q_2, a2_q} | {a1_q_2, a1_q};  // Or or_3, 8 bits wide
  assign and_3_out = {a2_q_2, a2_q} & {a1_q_2, a1_q};  // And and_3, 8 bits wide
  assign xor_1_out = {a2_q_2, a2_q} ^ {a1_q_2, a1_q};  // XOr xor_1, 8 bits wide
  BarrelShifter #(.Bits(8), .direction("right")) Right_shift (
    .in({a1_q_2, a1_q}), .shift(4'b0001), .out(Right_shift_out));
  // Probe ALU Input 1 on {a1_q_2, a1_q}
  // Probe ALU Input 2 on {a2_q_2, a2_q}
  PullDown pulldown_6 (.out(pulldown_6_out));
  Seven_Seg_Hex seven_seg_hex_7 (.d(a1_q_2), .dp(pulldown_7_out));
  Seven_Seg_Hex seven_seg_hex_8 (.d(a2_q_2), .dp(pulldown_7_out));
  Seven_Seg_Hex seven_seg_hex_9 (.d(a1_q), .dp(pulldown_7_out));
  Seven_Seg_Hex seven_seg_hex_10 (.d(a2_q), .dp(pulldown_7_out));
  PullDown pulldown_7 (.out(pulldown_7_out));
  // Pins of 1 and 8 bits meet at decoder_3_out_3

  // Notes on the sheet:
  //   RAM___ROM: Maps the first 8 K of the address space
  //   0 = ROM
  //   1 = RAM
  //   Control logic:
  //   Goal - Use only 2× 8KB ROM chips (12-inputs, 16-outputs)
  //   Control Logic Inputs, 12-bits:
  //    - Step (0,1,2,3,4,5,6,7) - 3-bits
  //    - Flags (zero, neg) - 2-bits
  //    - Instruction-register - Remaining 7 bits give 128 instructions
  //    - Can the extra instruction-bit be used for something useful?
  //   Control Logic Outputs:
  //     [12:15] - Data Bus Driver
  //               0 → r1
  //               1 → r2
  //               2 → r3
  //               3 → r4
  //               4 → ram
  //               5 → ah
  //               6 → al
  //               7 → add
  //               8 → add-c
  //               9 → sub
  //               a → sub-c
  //               b → or
  //               c → and
  //               d → xor
  //               e → rshift
  //               f → I/O
  //     [8:11]  - Data Bus Consumer
  //               0 → r1
  //               1 → r2
  //               2 → r3
  //               3 → r4
  //               4 → ram
  //               5 → dh
  //               6 → dl
  //               7 → a1
  //               8 → a2
  //               9 → none (Configuration register?)
  //               a → none
  //               b → none
  //               c → none
  //               d → none
  //               e → none
  //               f → I/O
  //     [6:7]   - Address Bus Driver
  //               0 → PC
  //               1 → DC
  //               2 → SP
  //               3 → DH/DL
  //     [3:5]   - Address Bus Consumer
  //               0 → PC
  //               1 → DC
  //               2 → SP
  //               3 → AH/AL
  //               4 → none
  //               5 → none
  //               6 → none
  //               7 → none
  //     [0:2]   - Misc
  //               0 → PC Count
  //               1 → DC Count
  //               2 → SP Increase
  //               3 → SP Decrease
  //               4 → none (I/O control?)
  //               5 → none
  //               6 → none
  //               7 → Instruction complete
  //   Data Driver
  //   Data Consumer
  //   Addr
  //   Driver
  //   Address
  //   Consumer
  //   Misc
  //   General Registers
  //   contents of _8_KB_ROM (hex, n*v repeats v):
  //   de,ad,be,ef
  //   Address Bus
  //   Data Bus
  //   ALU
  //   To Do:
  //    - Configuration register (ROM-enable, Blinkenlights-enable, halt, etc)
  //    - Flag register (Zero, Neg, Carry)
  //    - I/O
  //    - Instruction register
  //    - Control logic
  //   Notes:
  //    - Lshift can be implemented by adding a number to itself.
  //    - Invert can be implemented by XOR-ing with 0xff
  //    - Carry-in could be used to implement an Inc instruction
  //   Bootstrap Plan:
  //    1. ROM mapped at 0x0000-0x1fff
  //    2. Copy any required code to the end of ram
  //    3. Disable ROM and map RAM to full address space
endmodule
